// Logisim project Practica03.circ as structural Verilog: 8 circuits, main circuit main
module main (
);

  wire clock_1_out;
  wire [4:0] ildown_1_rd, ildown_1_rt, multiplexer_1_out;
  wire [31:0] alu_1_result, data_memory_1_read_data, fetch_1_instruction, fetch_1_pcplus4,
       reg_file_1_read_data1, reg_file_1_read_data2, shift_left2_1_out32bit, sign_ext_1_out32bit;

  Clock clock_1 (.out(clock_1_out));
  Fetch fetch_1 (.PCplus4(fetch_1_pcplus4), .Instruction(fetch_1_instruction));  // open: PCnext, CLK, Reset, PC
  Ildown ildown_1 (
    .Instruction(fetch_1_instruction), .rd(ildown_1_rd), .rt(ildown_1_rt));  // open: address, imm, funct, shamt, rs, op
  Sign_Ext sign_ext_1 (.Out32bit(sign_ext_1_out32bit));  // open: In16bit
  Multiplexer #(.width(5)) multiplexer_1 (.in0(ildown_1_rt), .in1(ildown_1_rd), .out(multiplexer_1_out));  // open: sel
  Shift_left2 shift_left2_1 (.In32bit(sign_ext_1_out32bit), .Out32bit(shift_left2_1_out32bit));
  Adder #(.width(32)) adder_1 (.a(fetch_1_pcplus4), .b(shift_left2_1_out32bit));  // open: out, cin, cout
  Reg_File reg_file_1 (
    .Read_Reg2(multiplexer_1_out), .Write_Data(data_memory_1_read_data), .CLK(clock_1_out),
    .Read_Data1(reg_file_1_read_data1), .Read_Data2(reg_file_1_read_data2));  // open: Read_Reg1, Reg_Write, Write_Reg, Reset
  ALU alu_1 (.In1(reg_file_1_read_data1), .Result(alu_1_result));  // open: In2, ALU_Operation, Zero
  Data_memory data_memory_1 (
    .Address(alu_1_result), .CLK(clock_1_out), .MemInput(reg_file_1_read_data2),
    .Read_data(data_memory_1_read_data));  // open: MemWrite, MemRead
endmodule

module Fetch (
  input  [31:0] PCnext,
  input  CLK,
  input  Reset,
  output [31:0] PC,
  output [31:0] PCplus4,
  output [31:0] Instruction
);

  Register #(.width(32)) PCreg (.D(PCnext), .en(1'b1), .clk(CLK), .Q(PC), .clr(Reset));
  // Probe on PC
  Adder #(.width(32)) adder_1 (.a(PC), .b(32'h4), .out(PCplus4));  // open: cin, cout
  ROM #(.addrWidth(24), .dataWidth(32)) rom_1 (.addr(PC[25:2]), .data(Instruction));
  // Probe on PC[25:2]
  // Probe on PCplus4
  // Probe on Instruction

  // Notes on the sheet:
  //   contents of rom_1 (hex, n*v repeats v):
  //   112345 0 cab4
endmodule

module Ildown (
  input  [31:0] Instruction,
  output [25:0] address,
  output [15:0] imm,
  output [5:0] funct,
  output [4:0] shamt,
  output [4:0] rd,
  output [4:0] rt,
  output [4:0] rs,
  output [5:0] op
);


  assign address = Instruction[25:0];
  assign funct = Instruction[5:0];
  assign imm = Instruction[15:0];
  assign op = Instruction[31:26];
  assign rd = Instruction[15:11];
  assign rs = Instruction[25:21];
  assign rt = Instruction[20:16];
  assign shamt = Instruction[10:6];
endmodule

module Reg_File (
  input  [4:0] Read_Reg1,
  input  [4:0] Read_Reg2,
  input  Reg_Write,
  input  [4:0] Write_Reg,
  input  [31:0] Write_Data,
  input  CLK,
  input  Reset,
  output [31:0] Read_Data1,
  output [31:0] Read_Data2
);

  wire decoder_1_out0, decoder_1_out1, decoder_1_out2, decoder_1_out3, decoder_1_out4, decoder_1_out5,
       decoder_1_out6, decoder_1_out7, decoder_1_out8, decoder_1_out9, decoder_1_out10, decoder_1_out11,
       decoder_1_out12, decoder_1_out13, decoder_1_out14, decoder_1_out15, decoder_1_out16, decoder_1_out17,
       decoder_1_out18, decoder_1_out19, decoder_1_out20, decoder_1_out21, decoder_1_out22, decoder_1_out23,
       decoder_1_out24, decoder_1_out25, decoder_1_out26, decoder_1_out27, decoder_1_out28, decoder_1_out29,
       decoder_1_out30, decoder_1_out31;
  wire [31:0] a0, a1, a2, a3, at, fp, gp, k0, k1, ra, s0, s1, s2, s3, s4, s5, s6, s7, sp, t0, t1, t2, t3, t4,
       t5, t6, t7, t8, t9, v0, v1, zero;

  Decoder #(.select(5)) decoder_1 (
    .out0(decoder_1_out0), .out1(decoder_1_out1), .out2(decoder_1_out2), .out3(decoder_1_out3),
    .out4(decoder_1_out4), .out5(decoder_1_out5), .out6(decoder_1_out6), .out7(decoder_1_out7),
    .out8(decoder_1_out8), .out9(decoder_1_out9), .out10(decoder_1_out10), .out11(decoder_1_out11),
    .out12(decoder_1_out12), .out13(decoder_1_out13), .out14(decoder_1_out14), .out15(decoder_1_out15),
    .out16(decoder_1_out16), .out17(decoder_1_out17), .out18(decoder_1_out18), .out19(decoder_1_out19),
    .out20(decoder_1_out20), .out21(decoder_1_out21), .out22(decoder_1_out22), .out23(decoder_1_out23),
    .out24(decoder_1_out24), .out25(decoder_1_out25), .out26(decoder_1_out26), .out27(decoder_1_out27),
    .out28(decoder_1_out28), .out29(decoder_1_out29), .out30(decoder_1_out30), .out31(decoder_1_out31),
    .sel(Write_Reg), .en(Reg_Write));
  Register #(.width(32)) u_zero (.D({32{1'b0}}), .en(decoder_1_out0), .clk(CLK), .Q(zero), .clr(Reset));
  Register #(.width(32)) u_t0 (.D(Write_Data), .en(decoder_1_out8), .clk(CLK), .Q(t0), .clr(Reset));
  Register #(.width(32)) u_s0 (.D(Write_Data), .en(decoder_1_out16), .clk(CLK), .Q(s0), .clr(Reset));
  Register #(.width(32)) u_t8 (.D(Write_Data), .en(decoder_1_out24), .clk(CLK), .Q(t8), .clr(Reset));
  Register #(.width(32)) u_at (.D(Write_Data), .en(decoder_1_out1), .clk(CLK), .Q(at), .clr(Reset));
  Register #(.width(32)) u_t1 (.D(Write_Data), .en(decoder_1_out9), .clk(CLK), .Q(t1), .clr(Reset));
  Register #(.width(32)) u_s1 (.D(Write_Data), .en(decoder_1_out17), .clk(CLK), .Q(s1), .clr(Reset));
  Register #(.width(32)) u_t9 (.D(Write_Data), .en(decoder_1_out25), .clk(CLK), .Q(t9), .clr(Reset));
  Register #(.width(32)) u_v0 (.D(Write_Data), .en(decoder_1_out2), .clk(CLK), .Q(v0), .clr(Reset));
  Register #(.width(32)) u_t2 (.D(Write_Data), .en(decoder_1_out10), .clk(CLK), .Q(t2), .clr(Reset));
  Register #(.width(32)) u_s2 (.D(Write_Data), .en(decoder_1_out18), .clk(CLK), .Q(s2), .clr(Reset));
  Register #(.width(32)) u_k0 (.D(Write_Data), .en(decoder_1_out26), .clk(CLK), .Q(k0), .clr(Reset));
  Register #(.width(32)) u_v1 (.D(Write_Data), .en(decoder_1_out3), .clk(CLK), .Q(v1), .clr(Reset));
  Register #(.width(32)) u_t3 (.D(Write_Data), .en(decoder_1_out11), .clk(CLK), .Q(t3), .clr(Reset));
  Register #(.width(32)) u_s3 (.D(Write_Data), .en(decoder_1_out19), .clk(CLK), .Q(s3), .clr(Reset));
  Register #(.width(32)) u_k1 (.D(Write_Data), .en(decoder_1_out27), .clk(CLK), .Q(k1), .clr(Reset));
  Register #(.width(32)) u_a0 (.D(Write_Data), .en(decoder_1_out4), .clk(CLK), .Q(a0), .clr(Reset));
  Register #(.width(32)) u_t4 (.D(Write_Data), .en(decoder_1_out12), .clk(CLK), .Q(t4), .clr(Reset));
  Register #(.width(32)) u_s4 (.D(Write_Data), .en(decoder_1_out20), .clk(CLK), .Q(s4), .clr(Reset));
  Register #(.width(32)) u_gp (.D(Write_Data), .en(decoder_1_out28), .clk(CLK), .Q(gp), .clr(Reset));
  Multiplexer #(.select(5), .width(32)) multiplexer_1 (
    .in0(zero), .in1(at), .in2(v0), .in3(v1), .in4(a0), .in5(a1), .in6(a2), .in7(a3), .in8(t0), .in9(t1),
    .in10(t2), .in11(t3), .in12(t4), .in13(t5), .in14(t6), .in15(t7), .in16(s0), .in17(s1), .in18(s2),
    .in19(s3), .in20(s4), .in21(s5), .in22(s6), .in23(s7), .in24(t8), .in25(t9), .in26(k0), .in27(k1),
    .in28(gp), .in29(sp), .in30(fp), .in31(ra), .out(Read_Data1), .sel(Read_Reg1));
  Multiplexer #(.select(5), .width(32)) multiplexer_2 (
    .in0(zero), .in1(at), .in2(v0), .in3(v1), .in4(a0), .in5(a1), .in6(a2), .in7(a3), .in8(t0), .in9(t1),
    .in10(t2), .in11(t3), .in12(t4), .in13(t5), .in14(t6), .in15(t7), .in16(s0), .in17(s1), .in18(s2),
    .in19(s3), .in20(s4), .in21(s5), .in22(s6), .in23(s7), .in24(t8), .in25(t9), .in26(k0), .in27(k1),
    .in28(gp), .in29(sp), .in30(fp), .in31(ra), .out(Read_Data2), .sel(Read_Reg2));
  Register #(.width(32)) u_a1 (.D(Write_Data), .en(decoder_1_out5), .clk(CLK), .Q(a1), .clr(Reset));
  Register #(.width(32)) u_t5 (.D(Write_Data), .en(decoder_1_out13), .clk(CLK), .Q(t5), .clr(Reset));
  Register #(.width(32)) u_s5 (.D(Write_Data), .en(decoder_1_out21), .clk(CLK), .Q(s5), .clr(Reset));
  Register #(.width(32)) u_sp (.D(Write_Data), .en(decoder_1_out29), .clk(CLK), .Q(sp), .clr(Reset));
  Register #(.width(32)) u_a2 (.D(Write_Data), .en(decoder_1_out6), .clk(CLK), .Q(a2), .clr(Reset));
  Register #(.width(32)) u_t6 (.D(Write_Data), .en(decoder_1_out14), .clk(CLK), .Q(t6), .clr(Reset));
  Register #(.width(32)) u_s6 (.D(Write_Data), .en(decoder_1_out22), .clk(CLK), .Q(s6), .clr(Reset));
  Register #(.width(32)) u_fp (.D(Write_Data), .en(decoder_1_out30), .clk(CLK), .Q(fp), .clr(Reset));
  Register #(.width(32)) u_a3 (.D(Write_Data), .en(decoder_1_out7), .clk(CLK), .Q(a3), .clr(Reset));
  Register #(.width(32)) u_t7 (.D(Write_Data), .en(decoder_1_out15), .clk(CLK), .Q(t7), .clr(Reset));
  Register #(.width(32)) u_s7 (.D(Write_Data), .en(decoder_1_out23), .clk(CLK), .Q(s7), .clr(Reset));
  Register #(.width(32)) u_ra (.D(Write_Data), .en(decoder_1_out31), .clk(CLK), .Q(ra), .clr(Reset));
endmodule

module ALU (
  input  [31:0] In1,
  input  [31:0] In2,
  input  [2:0] ALU_Operation,
  output Zero,
  output [31:0] Result
);

  wire Comp;
  wire [31:0] ADD, And_logic, Nor_logic, Or_logic, SUB;

  Adder #(.width(32)) adder_1 (.a(In1), .b(In2), .out(ADD));  // open: cin, cout
  Subtractor #(.width(32)) subtractor_1 (.a(In1), .b(In2), .out(SUB));  // open: bin, bout
  Comparator #(.width(32)) comparator_1 (.a(In1), .b(In2), .lt(Comp));  // open: gt, eq
  assign And_logic = In1 & In2;  // AND_Gate and_1, 32 bits wide
  assign Nor_logic = ~(In1 | In2);  // NOR_Gate nor_1, 32 bits wide
  assign Or_logic = In1 | In2;  // OR_Gate or_1, 32 bits wide
  Multiplexer #(.select(3), .width(32)) multiplexer_1 (
    .in0(And_logic), .in1(Or_logic), .in2(ADD), .in3(SUB), .in4({{31{1'b0}}, Comp}), .in5(Nor_logic),
    .out(Result), .sel(ALU_Operation));  // open: in6, in7
  Comparator #(.width(32)) comparator_2 (.a(Result), .b({32{1'b0}}), .eq(Zero));  // open: gt, lt

  // Other names for the same wires on the sheet: SLT[0] = Comp
endmodule

module Sign_Ext (
  input  [15:0] In16bit,
  output [31:0] Out32bit
);


  assign Out32bit = {{17{In16bit[15]}}, In16bit[14:0]};
endmodule

module Shift_left2 (
  input  [31:0] In32bit,
  output [31:0] Out32bit
);

  // Probe on In32bit
  // Probe on {In32bit[29:0], 2'b00}

  assign Out32bit = {In32bit[29:0], 2'b00};
endmodule

module Data_memory (
  input  [31:0] Address,
  input  MemWrite,
  input  MemRead,
  input  CLK,
  input  [31:0] MemInput,
  output [31:0] Read_data
);

  RAM #(.addrWidth(24), .asyncread("true"), .dataWidth(32)) ram_1 (
    .addr(Address[25:2]), .we(MemWrite), .oe(MemRead), .clk(CLK), .din(MemInput), .dout(Read_data));
endmodule
